# Fritzing sketch tea - Copy (saved by Fritzing 0.9.3b)
breadboards: 1

parts:
  Part1 = Arduino Uno (Rev3)
  J1 = Basic Servo
  DHT1 = DHT11 Humitidy and Temperature Sensor
  Water_Level_Sensor1 = Water Level Sensor
  Part2 = Adafruit DS3231 [part_number="Adafruit #3013"]
  U1 = 4-Channel 5v Relay Shield [package=relay-4ch5v10a]  # not connected
  F1 = Fan - Ventilador [package=THT]  # not connected
  WATER_PUMP1 = water pump/motor  # not connected
  F2 = Fan - Ventilador [package=THT]  # not connected
  LED1 = LEDs [package=led10mm]  # not connected
  Display1 = LCD screen 16x2 IIC [part_number=101290]

nets:
  N1: Part1.A1, Water_Level_Sensor1.SIG
  N2: Part1.A4/SDA, Part2.SDA, Display1.SDA
  N3: Part1.A5/SCL, Part2.SCL, Display1.SCL
  GND: Part1.GND, J1.gnd, DHT1.GND, Water_Level_Sensor1.GND, Part2.GND, Display1.GND
  N4: Part1.D3_PWM, J1.pulse
  VCC: Part1.3V3, J1.vcc, DHT1.VDD, DHT1.DATA, Water_Level_Sensor1.VCC, Part2.Vin, Display1.VCC

custom parts:
  DHT11 Humitidy and Temperature Sensor: DHT11 Humidity and Temperature Sensor
  Water Level Sensor: A water level sensor. This sensor operates at 3V to 5V. The Sig (signal) pin outputs an analogue signal that is in proportion to the amount of water in contact with the sensor.
  Adafruit DS3231: The datasheet for the DS3231 explains that this part is an "Extremely Accurate I²C-Integrated RTC/TCXO/Crystal". And, hey, it does exactly what it says on the tin! This Real Time Clock (RTC) is the most precise you can get in a small, low power package. Most RTCs use an external 32kHz timing crystal that is used to keep time with low current draw. And that's all well and good, but those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
  4-Channel 5v Relay Shield: 4 Channel 5v Relay Shield w. 2x SPD-06VDC-SD-C
  Fan - Ventilador: Ventilador de 2 pines, se encuentra comunmente en computadoras de escritorio
  water pump/motor: WATER PUMP BY ARDUBLOCKTR
  LEDs: LEDs Standard schematic elements and footprints for 5mm, 3mm, 1206, and 0603 sized LEDs. 5mm - Spark Fun Electronics SKU : COM-00529 (and others)
  LCD screen 16x2 IIC: LCD screen with HD44780 controller enables showing text, symbols, value or anything else that comes from Croduino/Arduino. It is capable of showing 16 symbols in two lines and therefore can be used in many projects that need to send clearly visible and legible output information.. • Color of symbols: White • Backlight: Blue • Dimensions: 80 x 36 x 12 mm • Screen dimensions: 64.5 x 16 mm •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
