# Fritzing sketch tea (saved by Fritzing 0.9.3b)
breadboards: 1

parts:
  Part1 = Arduino Uno (Rev3)
  J1 = Basic Servo
  DHT1 = DHT11 Humitidy and Temperature Sensor
  Water_Level_Sensor1 = Water Level Sensor
  Part2 = Adafruit DS3231 [part_number="Adafruit #3013"]
  F1 = Fan - Ventilador [package=THT]
  WATER_PUMP1 = water pump/motor  # not connected
  F2 = Fan - Ventilador [package=THT]
  LED1 = LEDs [package=led10mm]
  U1 = 4-Channel 5v Relay Shield [package=relay-4ch5v10a]
  J2 = 220v plug
  U2 = ESP8266 NodeMCU LoLin base

nets:
  N1: Part1.A1, Water_Level_Sensor1.SIG
  N2: Part1.A4/SDA, Part2.SDA
  N3: Part1.A5/SCL, Part2.SCL
  N4: Part1.D10_PWM/SS, U1.IN4
  N5: Part1.D11_PWM/MOSI, U1.IN3
  N6: Part1.D12/MISO, U1.IN2
  N7: Part1.D13/SCK, U1.IN1
  GND: Part1.GND, J1.gnd, DHT1.GND, Water_Level_Sensor1.GND, Part2.GND, U1.GND, U2.GND3-3, U2.GND8-10
  N8: Part1.D0/RX, U2.TX-0, U2.TX-2
  N9: Part1.D1/TX, U2.RX-0, U2.RX-2
  N10: Part1.D3_PWM, J1.pulse
  VCC: Part1.3V3, J1.vcc, DHT1.VDD, DHT1.DATA, Water_Level_Sensor1.VCC, Part2.Vin
  5V: Part1.5V, U1.VCC
  N11: F1.GND, U1.K2-On
  N12: F2.GND, U1.K3-On
  N13: LED1.A, J2.pin1
  N14: LED1.C, U1.K1-On
  N15: U1.K1-Off, J2.pin2

custom parts:
  DHT11 Humitidy and Temperature Sensor: DHT11 Humidity and Temperature Sensor
  Water Level Sensor: A water level sensor. This sensor operates at 3V to 5V. The Sig (signal) pin outputs an analogue signal that is in proportion to the amount of water in contact with the sensor.
  Adafruit DS3231: The datasheet for the DS3231 explains that this part is an "Extremely Accurate I²C-Integrated RTC/TCXO/Crystal". And, hey, it does exactly what it says on the tin! This Real Time Clock (RTC) is the most precise you can get in a small, low power package. Most RTCs use an external 32kHz timing crystal that is used to keep time with low current draw. And that's all well and good, but those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
  Fan - Ventilador: Ventilador de 2 pines, se encuentra comunmente en computadoras de escritorio
  water pump/motor: WATER PUMP BY ARDUBLOCKTR
  LEDs: LEDs Standard schematic elements and footprints for 5mm, 3mm, 1206, and 0603 sized LEDs. 5mm - Spark Fun Electronics SKU : COM-00529 (and others)
  4-Channel 5v Relay Shield: 4 Channel 5v Relay Shield w. 2x SPD-06VDC-SD-C
  220v plug: Generic 220V AC plug.
  ESP8266 NodeMCU LoLin base: ESP8266 based NodeMCU Base
