# Fritzing sketch tea2 (saved by Fritzing 0.9.3b)
breadboards: 1

parts:
  Part3 = Arduino Uno (Rev3)
  U3 = ESP8266 NodeMCU LoLin base
  J3 = 220v plug
  LED2 = LEDs [package=led10mm]
  F3 = Fan - Ventilador [package=THT]
  F4 = Fan - Ventilador [package=THT]
  WATER_PUMP2 = water pump/motor  # not connected
  J4 = Basic Servo
  DHT2 = DHT11 Humitidy and Temperature Sensor
  Water_Level_Sensor2 = Water Level Sensor
  Part4 = Adafruit DS3231 [part_number="Adafruit #3013"]
  U4 = 4-Channel 5v Relay Shield [package=relay-4ch5v10a]

nets:
  N1: Part3.A1, Water_Level_Sensor2.SIG
  N2: Part3.A4/SDA, Part4.SDA
  N3: Part3.A5/SCL, Part4.SCL
  N4: Part3.D10_PWM/SS, U4.IN4
  N5: Part3.D11_PWM/MOSI, U4.IN3
  N6: Part3.D12/MISO, U4.IN2
  N7: Part3.D13/SCK, U4.IN1
  GND: Part3.GND, U3.GND3-3, U3.GND8-10, J4.gnd, DHT2.GND, Water_Level_Sensor2.GND, Part4.GND, U4.GND
  N8: Part3.D0/RX, U3.TX-0, U3.TX-2
  N9: Part3.D1/TX, U3.RX-0, U3.RX-2
  N10: Part3.D3_PWM, J4.pulse
  VCC: Part3.D7, Part3.3V3, J4.vcc, DHT2.VDD, DHT2.DATA, Water_Level_Sensor2.VCC, Part4.Vin
  5V: Part3.5V, U4.VCC
  N11: J3.pin1, U4.K4-Off
  N12: LED2.A, U4.K4-On
  N13: F3.5V, U4.K1-On
  N14: F4.5V, U4.K2-On

custom parts:
  ESP8266 NodeMCU LoLin base: ESP8266 based NodeMCU Base
  220v plug: Generic 220V AC plug.
  LEDs: LEDs Standard schematic elements and footprints for 5mm, 3mm, 1206, and 0603 sized LEDs. 5mm - Spark Fun Electronics SKU : COM-00529 (and others)
  Fan - Ventilador: Ventilador de 2 pines, se encuentra comunmente en computadoras de escritorio
  water pump/motor: WATER PUMP BY ARDUBLOCKTR
  DHT11 Humitidy and Temperature Sensor: DHT11 Humidity and Temperature Sensor
  Water Level Sensor: A water level sensor. This sensor operates at 3V to 5V. The Sig (signal) pin outputs an analogue signal that is in proportion to the amount of water in contact with the sensor.
  Adafruit DS3231: The datasheet for the DS3231 explains that this part is an "Extremely Accurate I²C-Integrated RTC/TCXO/Crystal". And, hey, it does exactly what it says on the tin! This Real Time Clock (RTC) is the most precise you can get in a small, low power package. Most RTCs use an external 32kHz timing crystal that is used to keep time with low current draw. And that's all well and good, but those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
  4-Channel 5v Relay Shield: 4 Channel 5v Relay Shield w. 2x SPD-06VDC-SD-C
