# Fritzing sketch tea3 (saved by Fritzing 0.9.3b)
breadboards: 1

parts:
  Part5 = Arduino Uno (Rev3)
  U5 = 4-Channel 5v Relay Shield [package=relay-4ch5v10a]
  U6 = ESP8266 NodeMCU LoLin base
  J5 = 220v plug
  LED3 = LEDs [package=led10mm]
  F5 = Fan - Ventilador [package=THT]
  F6 = Fan - Ventilador [package=THT]
  WATER_PUMP3 = water pump/motor  # not connected
  J6 = Basic Servo  # not connected
  DHT3 = DHT11 Humitidy and Temperature Sensor
  Water_Level_Sensor3 = Water Level Sensor
  Part6 = Adafruit DS3231 [part_number="Adafruit #3013"]
  J7 = 220v plug
  Water_Level_Sensor4 = Water Level Sensor

nets:
  N1: Part5.A0, Water_Level_Sensor4.SIG
  N2: Part5.A1, Water_Level_Sensor3.SIG
  N3: Part5.A4/SDA, Part6.SDA
  N4: Part5.A5/SCL, Part6.SCL
  N5: Part5.D10_PWM/SS, U5.IN1
  N6: Part5.D11_PWM/MOSI, U5.IN2
  N7: Part5.D12/MISO, U5.IN3
  N8: Part5.D13/SCK, U5.IN4
  GND: Part5.GND, U5.GND, U6.GND3-3, U6.GND8-10, DHT3.GND, Water_Level_Sensor3.GND, Part6.GND, Water_Level_Sensor4.GND
  N9: Part5.D0/RX, U6.TX-0, U6.TX-2
  N10: Part5.D1/TX, U6.RX-0, U6.RX-2
  VCC: Part5.D7, Part5.3V3, DHT3.VDD, DHT3.DATA, Water_Level_Sensor3.VCC, Part6.Vin, Water_Level_Sensor4.VCC
  5V: Part5.5V, U5.VCC
  N11: U5.K1-Off, J7.pin1
  N12: U5.K1-On, F5.5V
  N13: U5.K2-On, F6.5V
  N14: U5.K4-Off, J5.pin1
  N15: U5.K4-On, LED3.A
  N16: J5.pin2, LED3.C
  N17: F5.GND, J7.pin2

custom parts:
  4-Channel 5v Relay Shield: 4 Channel 5v Relay Shield w. 2x SPD-06VDC-SD-C
  ESP8266 NodeMCU LoLin base: ESP8266 based NodeMCU Base
  220v plug: Generic 220V AC plug.
  LEDs: LEDs Standard schematic elements and footprints for 5mm, 3mm, 1206, and 0603 sized LEDs. 5mm - Spark Fun Electronics SKU : COM-00529 (and others)
  Fan - Ventilador: Ventilador de 2 pines, se encuentra comunmente en computadoras de escritorio
  water pump/motor: WATER PUMP BY ARDUBLOCKTR
  DHT11 Humitidy and Temperature Sensor: DHT11 Humidity and Temperature Sensor
  Water Level Sensor: A water level sensor. This sensor operates at 3V to 5V. The Sig (signal) pin outputs an analogue signal that is in proportion to the amount of water in contact with the sensor.
  Adafruit DS3231: The datasheet for the DS3231 explains that this part is an "Extremely Accurate I²C-Integrated RTC/TCXO/Crystal". And, hey, it does exactly what it says on the tin! This Real Time Clock (RTC) is the most precise you can get in a small, low power package. Most RTCs use an external 32kHz timing crystal that is used to keep time with low current draw. And that's all well and good, but those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
