# Fritzing sketch tea4 (saved by Fritzing 0.9.3b)
breadboards: 1

parts:
  Part7 = Arduino Uno (Rev3)
  U7 = 4-Channel 5v Relay Shield [package=relay-4ch5v10a]
  U8 = ESP8266 NodeMCU LoLin base
  J8 = 220v plug
  LED4 = LEDs [package=led10mm]
  F7 = Fan - Ventilador [package=THT]
  F8 = Fan - Ventilador [package=THT]
  WATER_PUMP4 = water pump/motor  # not connected
  J9 = Basic Servo
  DHT4 = DHT11 Humitidy and Temperature Sensor
  Water_Level_Sensor4 = Water Level Sensor
  Part8 = Adafruit DS3231 [part_number="Adafruit #3013"]
  J10 = 220v plug
  U9 = 2RelayModule
  LED5 = LEDs [package=led10mm]
  J11 = 220v plug

nets:
  N1: Part7.A1, Water_Level_Sensor4.SIG
  N2: Part7.A4/SDA, Part8.SDA
  N3: Part7.A5/SCL, Part8.SCL
  N4: Part7.D8, U7.IN1
  N5: Part7.D9_PWM, U7.IN2
  N6: Part7.D10_PWM/SS, U7.IN3
  N7: Part7.D11_PWM/MOSI, U7.IN4
  N8: Part7.D12/MISO, U9.IN1
  GND: Part7.GND, Part7.D0/RX, U7.GND, U8.TX-0, U8.TX-3, U8.GND3-0, U8.GND3-2, U8.GND3-3, U8.3V3-2, U8.3V3-3, U8.GND8-9, J9.gnd, DHT4.GND, Water_Level_Sensor4.GND, Part8.GND, U9.GND
  N9: Part7.D1/TX, U8.RX-0, U8.RX-2
  N10: Part7.D6_PWM, J9.pulse
  3V3: Part7.D7, Part7.3V3, DHT4.VDD, DHT4.DATA, Water_Level_Sensor4.VCC, Part8.Vin
  VCC: Part7.5V, U7.VCC, U9.IN2, U9.VCC
  N11: U7.K1-Off, J10.pin1
  N12: U7.K1-On, F7.5V
  N13: U7.K2-On, F8.5V
  N14: U7.K4-Off, J8.pin1
  N15: U7.K4-On, LED4.A
  N16: J8.pin2, LED4.C
  N17: F7.GND, J10.pin2
  N18: U9.NC1, J11.pin1
  N19: U9.NO1, LED5.C
  N20: LED5.A, J11.pin2

custom parts:
  4-Channel 5v Relay Shield: 4 Channel 5v Relay Shield w. 2x SPD-06VDC-SD-C
  ESP8266 NodeMCU LoLin base: ESP8266 based NodeMCU Base
  220v plug: Generic 220V AC plug.
  LEDs: LEDs Standard schematic elements and footprints for 5mm, 3mm, 1206, and 0603 sized LEDs. 5mm - Spark Fun Electronics SKU : COM-00529 (and others)
  Fan - Ventilador: Ventilador de 2 pines, se encuentra comunmente en computadoras de escritorio
  water pump/motor: WATER PUMP BY ARDUBLOCKTR
  DHT11 Humitidy and Temperature Sensor: DHT11 Humidity and Temperature Sensor
  Water Level Sensor: A water level sensor. This sensor operates at 3V to 5V. The Sig (signal) pin outputs an analogue signal that is in proportion to the amount of water in contact with the sensor.
  Adafruit DS3231: The datasheet for the DS3231 explains that this part is an "Extremely Accurate I²C-Integrated RTC/TCXO/Crystal". And, hey, it does exactly what it says on the tin! This Real Time Clock (RTC) is the most precise you can get in a small, low power package. Most RTCs use an external 32kHz timing crystal that is used to keep time with low current draw. And that's all well and good, but those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
  2RelayModule: 2 relay arduino module SONGLE SRD05VDC-SL-C
